// Logisim project control-logic.circ as structural Verilog: 1 circuit, main circuit control_logic
module control_logic (
  input  [31:0] Instruction,
  input  BrEq,
  input  BrLt,
  output PCSel,
  output RegWEn,
  output [2:0] ImmSel,
  output BrUn,
  output ASel,
  output BSel,
  output [3:0] ALUSel,
  output MemWEn,
  output [1:0] WBSel
);

  wire and_1_out, and_2_out, and_3_out, and_4_out, and_5_out, and_6_out, nor_1_out, nor_2_out, not_1_out,
       not_2_out, not_3_out, not_4_out, not_5_out, not_6_out, not_7_out, not_8_out, not_9_out, not_10_out,
       or_1_out, or_2_out;
  wire [15:0] rom_1_data;

  ROM #(.addrWidth(6), .dataWidth(16)) rom_1 (.data(rom_1_data));  // open: addr
  not not_1 (not_1_out, Instruction[4]);
  not not_2 (not_2_out, Instruction[6]);
  and and_1 (and_1_out, Instruction[4], Instruction[5]);
  not not_3 (not_3_out, Instruction[5]);
  or or_1 (or_1_out, Instruction[5], Instruction[6]);
  and and_2 (and_2_out, not_1_out, Instruction[5], not_2_out);
  not not_4 (not_4_out, or_1_out);
  or or_2 (or_2_out, Instruction[4], not_4_out);
  or or_3 (PCSel, and_2_out, and_1_out, not_3_out);
  or or_4 (RegWEn, Instruction[2], or_2_out);
  nor nor_1 (nor_1_out, Instruction[2], Instruction[3]);
  not not_5 (not_5_out, Instruction[4]);
  not not_6 (not_6_out, Instruction[6]);
  nor nor_2 (nor_2_out, Instruction[2], Instruction[4]);
  not not_7 (not_7_out, Instruction[4]);
  and and_3 (and_3_out, Instruction[2], Instruction[4]);
  and and_4 (and_4_out, nor_1_out, not_5_out, Instruction[5], not_6_out);
  and and_5 (and_5_out, Instruction[2], Instruction[4]);
  and and_6 (and_6_out, nor_2_out, Instruction[5], Instruction[6]);
  and and_7 (ImmSel[2], Instruction[2], not_7_out, Instruction[5], Instruction[6]);
  or or_5 (ImmSel[0], and_3_out, and_4_out);
  or or_6 (ImmSel[1], and_5_out, and_6_out);
  not not_8 (not_8_out, Instruction[2]);
  not not_9 (not_9_out, Instruction[3]);
  not not_10 (not_10_out, Instruction[4]);
  and and_8 (BrUn, not_8_out, not_9_out, not_10_out, Instruction[5], Instruction[6], Instruction[13]);

  // Other names for the same wires on the sheet: opcode[4:0] = Instruction[6:2]; func3[2:0] = Instruction[14:12];
  //   func7 = Instruction[30]

  // Notes on the sheet:
  //   INPUTS to your circuit
  //   Connect ROM Input here ->
  //   ROM FOR CONTROL LOGIC
  //   DON'T CHANGE THE LOCATIONS OF THE INPUTS AND OUTPUTS!
  //   This is only if you choose to do the ROM option
  //   CONNECT
  //   WIRE
  //   TO
  //   USE
  //   ROM
  //   OUTPUT from your circuit
  //   Reminder: If using ROM, use combinational logic for PCSel
endmodule
